# Fritzing sketch IMU-Arduino (saved by Fritzing 1.0.2b)

parts:
  Part1 = Arduino Uno (Rev3) - ICSP
  Part2 = InvenSense MPU6050

nets:
  N1: Part1.A4/SDA, Part2.SDA, Part2.XDA, Part2.XCL
  N2: Part1.A5/SCL, Part2.SCL
  5V: Part1.5V, Part2.VCC
  GND: Part1.GND, Part2.GND
